// Logisim project IT1601_U201614898_潘翔.circ as structural Verilog: 6 circuits, main circuit ◇单周期MIPS
module \单周期MIPS  (
);

  wire and_1_out, and_3_out, and_5_out, and_6_out, and_7_out, BGEZ, CLK, comparator_1_eq, comparator_2_eq,
       en_go, equal, Go, LH, mips_alu_2_equal, multiplexer_4_out, not_1_out, not_2_out, not_3_out, or_1_out,
       or_2_out, or_3_out, or_4_out, register_1_q, RST, SignedExt, SysCall, undriven, \硬布线控制器_1_alu_src ,
       \硬布线控制器_1_beq , \硬布线控制器_1_bne , \硬布线控制器_1_jal , \硬布线控制器_1_jmp , \硬布线控制器_1_jr , \硬布线控制器_1_memtoreg ,
       \硬布线控制器_1_memwrite , \硬布线控制器_1_regdst , \硬布线控制器_1_regwrite , \硬布线控制器_2_alu_src , \硬布线控制器_2_beq ,
       \硬布线控制器_2_bne , \硬布线控制器_2_jal , \硬布线控制器_2_jmp , \硬布线控制器_2_jr , \硬布线控制器_2_memtoreg ,
       \硬布线控制器_2_memwrite , \硬布线控制器_2_regdst , \硬布线控制器_2_regwrite , \硬布线控制器_2_syscall ;
  wire [1:0] ALU_Shamt;
  wire [3:0] \硬布线控制器_1_alu_op , \硬布线控制器_2_alu_op ;
  wire [4:0] multiplexer_5_out, multiplexer_6_out, multiplexer_7_out, multiplexer_8_out, multiplexer_12_out;
  wire [5:0] undriven_3, undriven_4;
  wire [15:0] multiplexer_15_out, \总周期数 , \无条件分支数 , \条件分支成功数 ;
  wire [27:2] rom_2_data;
  wire [31:0] a0, adder_1_out, adder_2_out, bit_extender_1_out, bit_extender_2_out, bit_extender_3_out,
       JR_MUX_1, LedData, mips_alu_2_result, multiplexer_1_out, multiplexer_2_out, multiplexer_3_out,
       multiplexer_9_out, multiplexer_10_out, multiplexer_11_out, multiplexer_13_out, multiplexer_14_out,
       multiplexer_16_out, PC_2_q, ram_2_data, rom_1_data, shifter_1_out, undriven_2;
  wire [31:26] rom_2_data_2;

  Button \u_总复位  (.out(RST));
  Button u_Go (.out(Go));
  Clock clock_1 (.out(CLK));
  Multiplexer #(.width(32), .enable("false")) multiplexer_1 (
    .in0(adder_1_out), .in1(adder_2_out), .out(multiplexer_1_out), .sel(or_2_out));
  Hex_Digit_Display hex_digit_display_1 (.value(LedData[27:24]));  // open: dp
  Hex_Digit_Display hex_digit_display_2 (.value(LedData[31:28]));  // open: dp
  Multiplexer #(.width(32), .enable("false")) multiplexer_2 (
    .in0(multiplexer_1_out), .in1(JR_MUX_1), .out(multiplexer_2_out), .sel(\硬布线控制器_1_jr ));
  not not_1 (not_1_out, equal);
  Register #(.width(1)) register_1 (.D(en_go), .en(en_go), .Q(register_1_q), .clk(CLK), .clr(Go));
  Hex_Digit_Display hex_digit_display_3 (.value(LedData[23:20]));  // open: dp
  Hex_Digit_Display hex_digit_display_4 (.value(LedData[19:16]));  // open: dp
  Register #(.width(32)) PC ();  // open: D, en, Q, clk, clr
  Multiplexer #(.width(32), .enable("false")) multiplexer_3 (
    .in0(multiplexer_2_out), .in1({4'b0000, rom_2_data, 2'b00}), .out(multiplexer_3_out), .sel(\硬布线控制器_1_jmp ));
  Multiplexer #(.enable("false")) multiplexer_4 (
    .in0(not_1_out), .in1(1'b0), .out(multiplexer_4_out), .sel(register_1_q));
  Hex_Digit_Display hex_digit_display_5 (.value(LedData[15:12]));  // open: dp
  Hex_Digit_Display hex_digit_display_6 (.value(LedData[11:8]));  // open: dp
  or or_1 (or_1_out, \硬布线控制器_1_jmp , \硬布线控制器_1_jr );
  and and_1 (and_1_out, or_1_out, multiplexer_4_out);
  Register #(.width(32)) PC_2 (.D(multiplexer_3_out), .en(multiplexer_4_out), .Q(PC_2_q), .clk(CLK), .clr(RST));
  Counter #(.width(16), .max('hffff)) counter_1 (
    .count(multiplexer_4_out), .Q(\总周期数 ), .clk(undriven), .clr(RST));  // open: load, D, carry
  Hex_Digit_Display hex_digit_display_7 (.value(LedData[7:4]));  // open: dp
  Hex_Digit_Display hex_digit_display_8 (.value(LedData[3:0]));  // open: dp
  Counter #(.width(16), .max('hffff)) counter_2 (
    .count(and_1_out), .Q(\无条件分支数 ), .clk(CLK), .clr(RST));  // open: load, D, carry
  ROM #(.addrWidth(10), .dataWidth(32)) rom_1 (.data(rom_1_data));  // open: addr, sel
  ROM #(.addrWidth(10), .dataWidth(32)) rom_2 (.data({rom_2_data_2, rom_2_data}));  // open: addr, sel
  Adder #(.width(32)) adder_1 (.a(undriven_2), .b(32'h4), .out(adder_1_out));  // open: cin, cout
  // Probe on \总周期数 
  // Probe on \无条件分支数 
  // Probe on \条件分支成功数 
  MIPS_Regifile mips_regifile_1 ();  // open: Din, Clk, R1, R2, WE, W_num, R1_num, R2_num
  Comparator #(.width(32)) comparator_1 (.a(JR_MUX_1), .b(32'ha), .eq(comparator_1_eq));  // open: gt, lt
  \硬布线控制器  \u_硬布线控制器_1  (
    .Func(rom_2_data[7:2]), .OP(rom_2_data_2), .ALU_OP(\硬布线控制器_1_alu_op ), .MemToReg(\硬布线控制器_1_memtoreg ),
    .MemWrite(\硬布线控制器_1_memwrite ), .ALU_SRC(\硬布线控制器_1_alu_src ), .RegWrite(\硬布线控制器_1_regwrite ),
    .SysCALL(SysCall), .SignedExt(SignedExt), .RegDst(\硬布线控制器_1_regdst ), .JR(\硬布线控制器_1_jr ),
    .JMP(\硬布线控制器_1_jmp ), .Beq(\硬布线控制器_1_beq ), .JAL(\硬布线控制器_1_jal ), .Bne(\硬布线控制器_1_bne ));
  Multiplexer #(.width(5), .enable("false")) multiplexer_5 (
    .in0(rom_2_data[27:23]), .in1(5'b00010), .out(multiplexer_5_out), .sel(SysCall));
  Multiplexer #(.width(5), .enable("false")) multiplexer_6 (
    .in0(rom_2_data[22:18]), .in1(rom_2_data[17:13]), .out(multiplexer_6_out), .sel(\硬布线控制器_1_regdst ));
  Multiplexer #(.width(5), .enable("false")) multiplexer_7 (
    .in0(multiplexer_6_out), .in1({5{1'b1}}), .out(multiplexer_7_out), .sel(\硬布线控制器_1_jal ));
  assign bit_extender_1_out = {{16{rom_2_data[17]}}, rom_2_data[17:2]};  // Bit_Extender bit_extender_1
  assign bit_extender_2_out = {{16{1'b0}}, rom_2_data[17:2]};  // Bit_Extender bit_extender_2
  and and_2 (equal, SysCall, comparator_1_eq);
  MIPS_ALU mips_alu_1 ();  // open: X, Y, AluOP, Equal, Result, Result_2, shamt
  Multiplexer #(.width(5), .enable("false")) multiplexer_8 (
    .in0(rom_2_data[22:18]), .in1(5'b00100), .out(multiplexer_8_out), .sel(SysCall));
  Multiplexer #(.width(32), .enable("false")) multiplexer_9 (
    .in0(bit_extender_1_out), .in1(bit_extender_2_out), .out(multiplexer_9_out), .sel(SignedExt));
  Comparator #(.width(32)) comparator_2 (.a(JR_MUX_1), .b(32'h22), .eq(comparator_2_eq));  // open: gt, lt
  RAM #(.addrWidth(10), .dataWidth(32), .bus("separate")) ram_1 ();  // open: addr, din, data, str, sel, clk, ld, clr
  Shifter #(.width(32)) shifter_1 (.in(bit_extender_1_out), .\dist (5'b00010), .out(shifter_1_out));
  Register #(.width(32)) register_2 (.D(a0), .en(and_3_out), .Q(LedData), .clk(CLK), .clr(RST));
  and and_3 (and_3_out, SysCall, comparator_2_eq);
  not not_2 (not_2_out, comparator_2_eq);
  MIPS_Regifile mips_regifile_2 (
    .Din(multiplexer_16_out), .Clk(CLK), .R1(JR_MUX_1), .R2(a0), .WE(\硬布线控制器_1_regwrite ),
    .W_num(multiplexer_7_out), .R1_num(multiplexer_5_out), .R2_num(multiplexer_8_out));
  Adder #(.width(32)) adder_2 (.a(shifter_1_out), .b(adder_1_out), .out(adder_2_out));  // open: cin, cout
  and and_4 (en_go, SysCall, not_2_out);
  \硬布线控制器  \u_硬布线控制器_2  (
    .Func(undriven_4), .OP(undriven_3), .ALU_OP(\硬布线控制器_2_alu_op ), .MemToReg(\硬布线控制器_2_memtoreg ),
    .MemWrite(\硬布线控制器_2_memwrite ), .ALU_SRC(\硬布线控制器_2_alu_src ), .RegWrite(\硬布线控制器_2_regwrite ),
    .SysCALL(\硬布线控制器_2_syscall ), .SignedExt(SignedExt), .RegDst(\硬布线控制器_2_regdst ), .JR(\硬布线控制器_2_jr ),
    .JMP(\硬布线控制器_2_jmp ), .Beq(\硬布线控制器_2_beq ), .JAL(\硬布线控制器_2_jal ), .Bne(\硬布线控制器_2_bne ));
  Multiplexer #(.width(32), .enable("false")) multiplexer_10 (
    .in0(a0), .in1(multiplexer_9_out), .out(multiplexer_10_out), .sel(\硬布线控制器_1_alu_src ));
  Multiplexer #(.width(32), .enable("false")) multiplexer_11 (
    .in0(multiplexer_10_out), .in1({32{1'b0}}), .out(multiplexer_11_out), .sel(BGEZ));
  not not_3 (not_3_out, mips_alu_2_equal);
  Multiplexer #(.select(2), .width(5), .enable("false")) multiplexer_12 (
    .in0(JR_MUX_1[4:0]), .in1(5'b10110), .in2(rom_2_data[12:8]), .out(multiplexer_12_out), .sel(ALU_Shamt));  // open: in3
  or or_2 (or_2_out, and_5_out, and_7_out, and_6_out);
  and and_5 (and_5_out, mips_alu_2_equal, \硬布线控制器_1_beq );
  and and_6 (and_6_out, not_3_out, \硬布线控制器_1_bne );
  and and_7 (and_7_out, BGEZ, or_3_out);
  or or_3 (or_3_out, mips_alu_2_equal, ~mips_alu_2_result[0]);  // OR_Gate
  MIPS_ALU mips_alu_2 (
    .X(JR_MUX_1), .Y(multiplexer_11_out), .AluOP(\硬布线控制器_1_alu_op ), .Equal(mips_alu_2_equal),
    .Result(mips_alu_2_result), .shamt(multiplexer_12_out));  // open: Result_2
  or or_4 (or_4_out, and_5_out, and_6_out);
  Counter #(.width(16), .max('hffff)) counter_3 (
    .count(or_4_out), .Q(\条件分支成功数 ), .clk(CLK), .clr(RST));  // open: load, D, carry
  Multiplexer #(.width(32), .enable("false")) multiplexer_13 (
    .in0(mips_alu_2_result), .in1(ram_2_data), .out(multiplexer_13_out), .sel(\硬布线控制器_1_memtoreg ));
  RAM #(.addrWidth(10), .dataWidth(32), .bus("separate")) ram_2 (
    .addr(mips_alu_2_result[11:2]), .din(a0), .data(ram_2_data), .str(\硬布线控制器_1_memwrite ), .clk(CLK),
    .clr(RST));  // open: sel, ld
  Multiplexer #(.width(32), .enable("false")) multiplexer_14 (
    .in0(multiplexer_13_out), .in1(adder_1_out), .out(multiplexer_14_out), .sel(\硬布线控制器_1_jal ));
  assign bit_extender_3_out = {{16{multiplexer_15_out[15]}}, multiplexer_15_out};  // Bit_Extender bit_extender_3
  Multiplexer #(.width(16), .enable("false")) multiplexer_15 (
    .in0(ram_2_data[15:0]), .in1(ram_2_data[31:16]), .out(multiplexer_15_out), .sel(mips_alu_2_result[3]));
  Multiplexer #(.width(32), .enable("false")) multiplexer_16 (
    .in0(multiplexer_14_out), .in1(bit_extender_3_out), .out(multiplexer_16_out), .sel(LH));

  // Other names for the same wires on the sheet: v0[31:0] = JR_MUX_1

  // Notes on the sheet:
  //   数码管输出应该用寄存器锁存，否则显示数据只能一闪而过
  //   可以通过项目增加Logisim库的方式将前几次实验完成的电路作为子电路引入到本电路中使用
  //   数码管输出
  //   指令存储器
  //   OP
  //   rs
  //   指令字
  //   contents of rom_1 (hex, n*v repeats v):
  //   20110001 8000c05 20110001 20120002 20130003 8000c09 20110001 20120002 20130003 8000c0d 20110001
  //   20120002 20130003 8000c11 20110001 20120002 20130003 c000cb8 20100001 20110001 118fc0 112020
  //   20020022 c 118882 12200001 8000c15 112020 20020022 c 20110001 118880 112020 20020022 c 12200001
  //   8000c1f 20110001 118fc0 112020 20020022 c 1188c3 112020 20020022 c 118903 112020 20020022 c 118903
  //   112020 20020022 c 118903 112020 20020022 c 118903 112020 20020022 c 118903 112020 20020022 c 118903
  //   112020 20020022 c 118903 112020 20020022 c 20100001 109fc0 139fc3 8021 2012000c 24160003 26100001
  //   3210000f 20080008 20090001 139900 2709825 132020 20020022 c 1094022 1500fff9 22100001 2018000f
  //   2188024 108700 20080008 20090001 139902 2709825 132021 20020022 c 1094022 1500fff9 108702 2c9b022
  //   12c00001 8000c50 4020 1084027 84400 3508ffff 82021 20020022 c 2010ffff 20110000 ae300000 22100001
  //   22310004 ae300000 22100001 22310004 ae300000 22100001 22310004 ae300000 22100001 22310004 ae300000
  //   22100001 22310004 ae300000 22100001 22310004 ae300000 22100001 22310004 ae300000 22100001 22310004
  //   ae300000 22100001 22310004 ae300000 22100001 22310004 ae300000 22100001 22310004 ae300000 22100001
  //   22310004 ae300000 22100001 22310004 ae300000 22100001 22310004 ae300000 22100001 22310004 ae300000
  //   22100001 22310004 22100001 8020 2011003c 8e130000 8e340000 274402a 11000002 ae330000 ae140000
  //   2231fffc 1611fff8 102020 20020022 c 22100004 2011003c 1611fff2 2002000a c 20100000 22100001 102020
  //   20020022 c 22100002 102020 20020022 c 22100003 102020 20020022 c 22100004 102020 20020022 c 22100005
  //   102020 20020022 c 22100006 102020 20020022 c 22100007 102020 20020022 c 22100008 102020 20020022
  //   20020022 c 3e00008
  //   rt
  //   rd
  //   指令存储器
  //   Func
  //   指令字
  //   contents of rom_2 (hex, n*v repeats v):
  //   20110001 8000c05 20110001 20120002 20130003 8000c09 20110001 20120002 20130003 8000c0d 20110001
  //   20120002 20130003 8000c11 20110001 20120002 20130003 c000cbb 20100001 20110001 118fc0 112020
  //   20020022 c 118882 12200001 8000c15 112020 20020022 c 20110001 118880 112020 20020022 c 12200001
  //   8000c1f 20110001 118fc0 112020 20020022 c 1188c3 112020 20020022 c 118903 112020 20020022 c 118903
  //   112020 20020022 c 118903 112020 20020022 c 118903 112020 20020022 c 118903 112020 20020022 c 118903
  //   112020 20020022 c 118903 112020 20020022 c 20100001 109fc0 139fc3 8021 2012000c 24160003 26100001
  //   3210000f 20080008 20090001 139900 2709825 132020 20020022 c 1094022 1500fff9 22100001 2018000f
  //   2188024 108700 20080008 20090001 139902 2709825 132021 20020022 c 1094022 1500fff9 108702 2c9b022
  //   12c00001 8000c50 4020 1084027 84400 3508ffff 82021 20020022 c 2010ffff 20110000 ae300000 22100001
  //   22310004 ae300000 22100001 22310004 ae300000 22100001 22310004 ae300000 22100001 22310004 ae300000
  //   22100001 22310004 ae300000 22100001 22310004 ae300000 22100001 22310004 ae300000 22100001 22310004
  //   ae300000 22100001 22310004 ae300000 22100001 22310004 ae300000 22100001 22310004 ae300000 22100001
  //   22310004 ae300000 22100001 22310004 ae300000 22100001 22310004 ae300000 22100001 22310004 ae300000
  //   22100001 22310004 22100001 8020 2011003c 8e130000 8e340000 274402a 11000002 ae330000 ae140000
  //   2231fffc 1611fff8 102020 20020022 c 22100004 2011003c 1611fff2 20020032 c 8000c00 2002000a c
  //   20100000 22100001 102020 20020022 c 22100002 102020 20020022 c 22100003 102020 20020022 c 22100004
  //   102020 20020022 c 22100005 102020 20020022 c 22100006 102020 20020022 c 22100007 102020 20020022 c
  //   22100008 102020 20020022 20020022 c 3e00008
  //   总复位信号应将除ROM以外所有存储组件全部清零
  //   JMP
  //   JR
  //   OP
  //   Func
  //   OP
  //   Func
  //   rs
  //   rt
  //   rd
  //   立即数
  //   Beq
  //   Bne
  //   MemToReg
  //   MemWrite
  //   AluOP
  //   AluSrcB
  //   RegWrite
  //   JAL
  //   RegDst
  //   Syscall
  //   JMP
  //   JR
  //   OP
  //   Func
  //   Beq
  //   Bne
  //   MemToReg
  //   MemWrite
  //   AluOP
  //   AluSrcB
  //   RegWrite
  //   JAL
  //   RegDst
  //   Syscall
endmodule

// 单周期硬布线控制器
module \硬布线控制器  (
  input  [5:0] OP,
  input  [5:0] Func,
  output [3:0] ALU_OP,
  output MemToReg,
  output MemWrite,
  output ALU_SRC,
  output RegWrite,
  output SysCALL,
  output SignedExt,
  output RegDst,
  output Beq,
  output Bne,
  output JR,
  output JMP,
  output JAL
);

  \运算控制器  \u_运算控制器_1  (
    .OP0(OP[0]), .OP1(OP[1]), .OP2(OP[2]), .OP3(OP[3]), .OP4(OP[4]), .OP5(OP[5]), .F0(Func[0]), .F1(Func[1]),
    .F2(Func[2]), .F3(Func[3]), .F4(Func[4]), .F5(Func[5]), .S0(ALU_OP[0]), .S1(ALU_OP[1]), .S2(ALU_OP[2]),
    .S3(ALU_OP[3]));
  \控制信号生成  \u_控制信号生成_1  (
    .OP0(OP[0]), .OP1(OP[1]), .OP2(OP[2]), .OP3(OP[3]), .OP4(OP[4]), .OP5(OP[5]), .F0(Func[0]), .F1(Func[1]),
    .F2(Func[2]), .F3(Func[3]), .F4(Func[4]), .F5(Func[5]), .MemToReg(MemToReg), .MemWrite(MemWrite),
    .ALU_SRC(ALU_SRC), .RegWrite(RegWrite), .SysCALL(SysCALL), .SignedExt(SignedExt), .RegDst(RegDst),
    .BEQ(Beq), .BNE(Bne), .JR(JR), .JMP(JMP), .JAL(JAL));

  // Other names for the same wires on the sheet: OP_CODE[5:0] = OP

  // Notes on the sheet:
  //   运算器控制器，根据指令生成运算器功能选择信号
  //   控制信号生成，产生数据通路需要的其他控制信号
endmodule

// 运算器控制器
module \运算控制器  (
  input  OP0,
  input  OP1,
  input  OP2,
  input  OP3,
  input  OP4,
  input  OP5,
  input  F0,
  input  F1,
  input  F2,
  input  F3,
  input  F4,
  input  F5,
  output S0,
  output S1,
  output S2,
  output S3
);
endmodule

// 控制信号生成
module \控制信号生成  (
  input  OP0,
  input  OP1,
  input  OP2,
  input  OP3,
  input  OP4,
  input  OP5,
  input  F0,
  input  F1,
  input  F2,
  input  F3,
  input  F4,
  input  F5,
  output MemToReg,
  output MemWrite,
  output ALU_SRC,
  output RegWrite,
  output SysCALL,
  output SignedExt,
  output RegDst,
  output BEQ,
  output BNE,
  output JR,
  output JMP,
  output JAL
);
endmodule

// ALU
module MIPS_ALU (
  input  [4:0] shamt,
  input  [31:0] X,
  input  [31:0] Y,
  input  [3:0] AluOP,
  output Equal,
  output [31:0] Result,
  output [31:0] Result_2
);

  wire [0:0] comparator_1_lt, comparator_2_lt;
  wire [31:0] adder_1_out, AND_out, divider_1_out, divider_1_rem, multiplier_1_cout, multiplier_1_out,
       NOR_out, OR_out, shifter_1_out, shifter_2_out, shifter_3_out, subtractor_1_out, XOR_out;

  assign AND_out = X & Y;  // AND_Gate AND, 32 bits wide
  assign OR_out = X | Y;  // OR_Gate OR, 32 bits wide
  Shifter #(.width(32)) shifter_1 (.in(Y), .\dist (shamt), .out(shifter_1_out));
  Shifter #(.width(32), .shift("ar")) shifter_2 (.in(Y), .\dist (shamt), .out(shifter_2_out));
  Shifter #(.width(32), .shift("lr")) shifter_3 (.in(Y), .\dist (shamt), .out(shifter_3_out));
  Multiplier #(.width(32)) multiplier_1 (.a(X), .b(Y), .out(multiplier_1_out), .cout(multiplier_1_cout));  // open: cin
  Divider #(.width(32)) divider_1 (.a(X), .b(Y), .out(divider_1_out), .rem(divider_1_rem));  // open: upper
  Adder #(.width(32)) adder_1 (.a(X), .b(Y), .out(adder_1_out));  // open: cin, cout
  Subtractor #(.width(32)) subtractor_1 (.a(X), .b(Y), .out(subtractor_1_out));  // open: bin, bout
  assign XOR_out = X ^ Y;  // XOR_Gate XOR, 32 bits wide
  assign NOR_out = ~(X | Y);  // NOR_Gate NOR, 32 bits wide
  Comparator #(.width(32)) comparator_1 (.a(X), .b(Y), .eq(Equal), .lt(comparator_1_lt[0]));  // open: gt
  Comparator #(.width(32), .mode("unsigned")) comparator_2 (.a(X), .b(Y), .lt(comparator_2_lt[0]));  // open: gt, eq
  Multiplexer #(.select(4), .width(32), .enable("false")) multiplexer_1 (
    .in0(shifter_1_out), .in1(shifter_2_out), .in2(shifter_3_out), .in3(multiplier_1_out),
    .in4(divider_1_out), .in5(adder_1_out), .in6(subtractor_1_out), .in7(AND_out), .in8(OR_out),
    .in9(XOR_out), .in10(NOR_out), .in11({{31{1'b0}}, comparator_1_lt[0]}),
    .in12({{31{1'b0}}, comparator_2_lt[0]}), .in13({32{1'b0}}), .in14({32{1'b0}}), .in15({32{1'b0}}),
    .out(Result), .sel(AluOP));
  Multiplexer #(.select(4), .width(32), .enable("false")) multiplexer_2 (
    .in0({32{1'b0}}), .in1({32{1'b0}}), .in2({32{1'b0}}), .in3(multiplier_1_cout), .in4(divider_1_rem),
    .in5({32{1'b0}}), .in6({32{1'b0}}), .in7({32{1'b0}}), .in8({32{1'b0}}), .in9({32{1'b0}}),
    .in10({32{1'b0}}), .in11({32{1'b0}}), .in12({32{1'b0}}), .in13({32{1'b0}}), .in14({32{1'b0}}),
    .in15({32{1'b0}}), .out(Result_2), .sel(AluOP));

  // Other names for the same wires on the sheet: Result2[31:0] = Result_2; S[3:0] = AluOP

  // Notes on the sheet:
  //   不要改变此引脚区域内容，也不要改变ALU封装形式
  //   输入引脚
  //   输出引脚
endmodule

module MIPS_Regifile (
  input  [31:0] Din,
  input  Clk,
  input  WE,
  input  [4:0] R1_num,
  input  [4:0] W_num,
  input  [4:0] R2_num,
  output [31:0] R1,
  output [31:0] R2
);

  // RegisterFile registerfile_1: pin names not known; wires that end beside it: Din, Clk, WE, W_num, R1_num, R2_num, R1, R2
endmodule
